# Fritzing sketch meda1027_info1lab_morsedecoder (saved by Fritzing 0.9.4)
breadboards: 1

parts:
  U2 = ESP32S-HiLetgo [part_number=ESP32S-HiLetgo]
  S1 = Round Pushbutton
  Nokia_5110_LCD_Module1 = Nokia 5110 LCD basado en PCD8544
  LED1 = smd LED [color="Red (633nm)" package="0603 [SMD]"]
  SG1 = Piezo [package=buzzer-12mm-ns-kit]
  R2 = Resistor [tolerance=±5% resistance=220 package="1206 [SMD]"]

nets:
  N1: U2.3.3, Nokia_5110_LCD_Module1.VCC
  GND: U2.GND, S1.leg1, Nokia_5110_LCD_Module1.GND, R2.Pin_1
  N2: U2.GPIO2, Nokia_5110_LCD_Module1.CE
  N3: U2.GPIO0, Nokia_5110_LCD_Module1.LIGHT
  N4: U2.GPIO4, S1.leg0
  N5: U2.GPIO17, Nokia_5110_LCD_Module1.RST
  N6: U2.GPIO5, LED1.anode, SG1.1
  N7: U2.GPIO18, Nokia_5110_LCD_Module1.CLK
  N8: U2.GPIO19, Nokia_5110_LCD_Module1.DC
  N9: U2.GPIO23, Nokia_5110_LCD_Module1.DIN
  N10: LED1.cathode, SG1.2, R2.Pin_0

custom parts:
  ESP32S-HiLetgo: HiLetgo ESP-WROOM-32 ESP32 ESP-32S Development Board 2.4GHz Dual-Mode WiFi + Bluetooth Dual Cores Microcontroller The ESP32 integrated with Antenna switches, RF Balun, power amplifiers, low-noise amplifiers, filters, and management modules, and the entire solution occupies the least area of PCB. 2.4 GHz Wi-Fi plus Bluetooth dual-mode chip, with TSMC Ultra-low power consumption 40nm technology,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
  Nokia 5110 LCD basado en PCD8544: Módulo Nokia 5110 LCD basado en el controlador PCD8544. Versión de 8 pines (sólo entrada).
  Piezo: Buzzer Spark Fun Electronics SIK for MicroView
